# Fritzing sketch scheme1 (saved by Fritzing 0.9.3b)

parts:
  Part1 = Arduino Nano (Rev3.0)
  R1 = TRIMPOT [package=3386u]
  U1 = WS2812 RGB LED strip
  C1 = Capacitor Polarized [package=panasonic_e]
  C2 = Capacitor Polarized [package=nippon_f80]
  R3 = Resistor [tolerance=±5% resistance=10k package=THT]
  Part2 = Adafruit MAX9814 Electret Microphone Amplifier [part_number="Adafruit #1713"]
  IR2 = tl1838 [package=THT]
  S1 = Momentary Switch [package=ksa_sealed_tac_switch]
  R4 = Resistor [tolerance=±5% resistance=100 package=THT]
  R5 = Resistor [tolerance=±5% resistance=1k package=THT]
  LED1 = LED - 3mm [color="Red (633nm)" package="3 mm [THT]"]  # not connected
  R6 = Resistor [tolerance=±5% resistance=1k package=THT]
  LED2 = LED - 3mm [color="Blue (525nm)" package="3 mm [THT]"]  # not connected
  R7 = Resistor [tolerance=±5% resistance=1k package=THT]
  LED3 = LED - 3mm [color="Green (570nm)" package="3 mm [THT]"]  # not connected

nets:
  GND: Part1.GND, IR2.GND, S1.2
  N1: Part1.D2, IR2.OUT
  N2: Part1.D6, R4.Pin_1
  N3: Part1.D7, S1.4
  N4: Part1.D9, R6.Pin_0
  N5: Part1.D10, R7.Pin_0
  VCC: Part1.5V, U1.VCC, C1.+, IR2.VCC
  N6: Part1.A0, R3.Pin_1
  N7: Part1.AREF, R1.WIPER
  N8: Part1.3V3, R1.CW
  N9: Part1.D13/SCK, R5.Pin_1
  GND_2: R1.CCW, U1.GND, C1.-, Part2.GND
  N10: U1.DIN, R4.Pin_0
  N11: C2.+, Part2.OUTPUT

custom parts:
  WS2812 RGB LED strip: WS2812 strip
  Adafruit MAX9814 Electret Microphone Amplifier: Add an ear to your project with this well-designed electret microphone amplifier with AGC. This fully assembled and tested board comes with a 20-20KHz electret microphone soldered on. For the amplification, we use the Maxim MAX9814, a specialty chip that is designed for amplifying electret microphones in situations where the loudness of the audio isn't predictable. This fancy microphone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
  tl1838: The TL1838 is a miniaturized receiver for infrared remote control systems. A PIN diode and a preamplifier are assembled on a lead frame, the epoxy package acts as an IR filter. The demodulated output signal can be directly decoded by a microprocessor.
